# Fritzing sketch papilio-dsp-wing-v1.2 (saved by Fritzing 0.9.3b)
circuit board: 7.18775cm x 2.75735cm
stripboards: 1

parts:
  IC = IC, DIP package, 16 pins [chip_label=MCP3208]
  R1 = Trimmer Potentiometer [maximum_resistance=10kΩ package=THT]
  U2 = 2.5mm Audio Jack [package=stereojack2.5mm_specia_pogopins]
  C2 = Capacitor Polarized [package=cpol-radial-10uf-25v]
  S1 = Toggle Switch [package=THT]
  IC1 = IC, DIP package, 8 pins [chip_label=LM386]
  J1 = male pin header, 4 pins [form="♂ (male)"]
  J2 = male pin header, 8 pins [form="♂ (male)"]
  C1 = Capacitor Polarized [package=cpol-radial-10uf-25v]

nets (from the schematic view):
  N1: IC.pin1, S1.COM
  GND: IC.pin9, IC.pin14, R1.leg2, U2.SLEEVE, IC1.pin2, IC1.pin4, J1.pin1
  N2: IC.pin10, J2.pin4
  N3: IC.pin11, J2.pin2
  N4: IC.pin12, J2.pin3
  N5: IC.pin13, J2.pin1
  N6: IC.pin15, R1.wiper
  VCC: IC.pin16, R1.leg1, IC1.pin6, J1.pin4
  N7: U2.LEFT, U2.RIGHT, C2.+
  N8: C2.-, S1.L2, IC1.pin3
  N9: S1.L1, IC1.pin5
  N10: IC1.pin1, C1.+
  N11: IC1.pin8, C1.-

notes:
  PapilioDSP/Shred wing, An expansion module containing a 12bit ADC and an optional pre-amplifer circuit, 1.1
  Papilio wing connector
